# Fritzing sketch DataConsumer (saved by Fritzing 0.9.9b)

parts:
  U4 = ESP8266 ESP-01 Upgraded WiFi Module [part_number=ESP8266]
  Power_plug5 = Power plug
  Power_plug6 = Power plug
  U5 = Graphical LCD 128x64 [package=lcd-g12864]  # not connected
  Componente1 = Arduino Uno (Rev3)
  Raspberry_Pi_A1 = Raspberry Pi A

nets:
  N1: U4.RXD, Componente1.D1/TX
  VCC: U4.VCC, U4.CH_PD, Power_plug6.VCC
  GND: U4.GND, Power_plug5.GND, Power_plug6.GND
  N2: U4.TXD, Componente1.D0/RX
  VCC_2: Power_plug5.VCC, Componente1.VIN
  N3: Componente1.A4/SDA, Raspberry_Pi_A1.GPIO_2
  N4: Componente1.A5/SCL, Raspberry_Pi_A1.GPIO_3

notes:
  3.3v
  LCD Screen 128x64
  TX
  RX
  VIN
  GND
  5v
  ESP-01

custom parts:
  ESP8266 ESP-01 Upgraded WiFi Module: Upgraded Version ESP-01,all Flash are upgraded to 1M byte.Also support Cloud service remote transmission.
