# Fritzing sketch DataProducer1 (saved by Fritzing 0.9.9b)

parts:
  U2 = ESP8266 ESP-01 Upgraded WiFi Module [part_number=ESP8266]
  Power_plug3 = Power plug
  Power_plug4 = Power plug
  U3 = Graphical LCD 128x64 [package=lcd-g12864]  # not connected
  DHT1 = DHT11 Humitidy and Temperature Sensor

nets:
  VCC: U2.VCC, U2.CH_PD, Power_plug4.VCC
  N1: U2.GPIO_2, DHT1.DATA
  GND: U2.GND, Power_plug3.GND, Power_plug4.GND, DHT1.GND
  VCC_2: Power_plug3.VCC, DHT1.VDD

notes:
  3.3v
  LCD Screen 128x64
  GND
  5v
  ESP-01
  VIN
  TX
  RX
  DHT11

custom parts:
  ESP8266 ESP-01 Upgraded WiFi Module: Upgraded Version ESP-01,all Flash are upgraded to 1M byte.Also support Cloud service remote transmission.
  DHT11 Humitidy and Temperature Sensor: DHT11 Humidity and Temperature Sensor
