# Fritzing sketch DataProducer2 (saved by Fritzing 0.9.9b)

parts:
  U1 = ESP8266 ESP-01 Upgraded WiFi Module [part_number=ESP8266]
  Componente1 = Triple Axis Accelerometer Breakout - ADXL345
  LCD1 = LCD screen
  LCM1602_IIC1 = LCM1602 IIC [part_number="LCM1602 IIC" chip_label="LCM1602 IIC" package="DIP (Dual Inline) [THT]"]
  Power_plug1 = Power plug
  Power_plug2 = Power plug

nets:
  VCC: U1.VCC, U1.CH_PD, Power_plug1.VCC
  N1: U1.GPIO_0, Componente1.SDA, LCM1602_IIC1.SDA
  N2: U1.GPIO_2, Componente1.SCL, LCM1602_IIC1.SCL
  GND: U1.GND, Componente1.GND, LCM1602_IIC1.GND, Power_plug1.GND, Power_plug2.GND
  VCC_2: Componente1.VCC, LCM1602_IIC1.VCC, Power_plug2.VCC
  VSS: LCD1.VSS, LCM1602_IIC1.VSS
  VDD: LCD1.VDD, LCM1602_IIC1.VDD
  N3: LCD1.V0, LCM1602_IIC1.V0
  N4: LCD1.RS, LCM1602_IIC1.RS
  N5: LCD1.R/W, LCM1602_IIC1.RW
  N6: LCD1.E, LCM1602_IIC1.E
  N7: LCD1.DB0, LCM1602_IIC1.D0
  N8: LCD1.DB1, LCM1602_IIC1.D1
  N9: LCD1.DB2, LCM1602_IIC1.D2
  N10: LCD1.DB3, LCM1602_IIC1.D3
  N11: LCD1.DB4, LCM1602_IIC1.D4
  N12: LCD1.DB5, LCM1602_IIC1.D5
  N13: LCD1.DB6, LCM1602_IIC1.D6
  N14: LCD1.DB7, LCM1602_IIC1.D7
  N15: LCD1.LED+, LCM1602_IIC1.A
  N16: LCD1.LED-, LCM1602_IIC1.K
  N17: LCM1602_IIC1.LED_A, LCM1602_IIC1.LED_B

notes:
  3.3v
  ESP-01
  5v
  ADXL345
  PCF8574
  LCD Display 16x2

custom parts:
  ESP8266 ESP-01 Upgraded WiFi Module: Upgraded Version ESP-01,all Flash are upgraded to 1M byte.Also support Cloud service remote transmission.
  LCM1602 IIC: I2C-Module to use a 1602 or 2004 LCD on with the wire.h libory Serial LCD Modul
