# Fritzing sketch MQTT (saved by Fritzing 0.9.9b)
breadboards: 1

parts:
  U1 = ESP8266 NodeMCU LoLin base
  U2 = MCP23017 [package=dil28-3]
  LED1 = LED - 5mm [color="Red (633nm)" current=0.030 package="5 mm [THT]"]
  LED2 = LED - 5mm [color="Red (633nm)" current=0.030 package="5 mm [THT]"]
  LED3 = LED - 5mm [color="Red (633nm)" current=0.030 package="5 mm [THT]"]
  LED4 = LED - 5mm [color="Yellow (585nm)" current=0.030 package="5 mm [THT]"]
  LED5 = LED - 5mm [color="Yellow (585nm)" current=0.030 package="5 mm [THT]"]
  LED6 = LED - 5mm [color="Green (570nm)" current=0.030 package="5 mm [THT]"]

nets:
  N1: U1.3V1-0, U2.VCC, U2.RESET
  N2: U1.D1-3, U2.SCL
  N3: U1.D2-0, U1.D2-3, U2.SDA
  N4: U1.GND3-2, U1.GND8-0, U1.GND8-11, U2.GND, U2.A0, U2.A1, U2.A2, LED1.cathode, LED2.cathode, LED3.cathode, LED4.cathode, LED5.cathode, LED6.cathode
  N5: U2.GPA0, LED6.anode
  N6: U2.GPA1, LED5.anode
  N7: U2.GPA2, LED4.anode
  N8: U2.GPA3, LED3.anode
  N9: U2.GPA4, LED2.anode
  N10: U2.GPA5, LED1.anode

custom parts:
  ESP8266 NodeMCU LoLin base: ESP8266 based NodeMCU Base
  MCP23017: 16 bit I/O chip controlled via I2C
